# Fritzing sketch totem_fritzing_diagram (saved by Fritzing 0.9.4)
breadboards: 1

parts:
  Part10 = Arduino Mega 2560 (Rev3)
  YwRobot_Power_Supply1 = YwRobot Breadboard Power Supply [part_number=545043]
  7LEDDiskDFR3 = 7LEDDiskDFR0106
  7LEDDiskDFR4 = 7LEDDiskDFR0106
  J3 = GPS Module
  U2 = LCD-16X2 [package=lcd-16x2_noholes]
  ZS-042_RTC3 = ZS-042 RTC Module
  Part11 = Gravity Analog Sound Level Meter
  Part12 = KY-022 Infrared Receiver Module [package="Breakout board"]
  R4 = Resistor [tolerance=±5% resistance=220 package=THT]
  R5 = Trimmer Potentiometer [maximum_resistance=10kΩ package=THT]
  SdModule2 = SdModule
  Keypad4x1 = Membran Keypad 4x4

nets:
  N1: Part10.A1, Part11.A
  N2: Part10.D21/SCL, ZS-042_RTC3.SCL
  N3: Part10.D20/SDA, ZS-042_RTC3.SDA
  N4: Part10.D19/RX1, J3.TX_(Blue)
  N5: Part10.D18/TX1, J3.RX_(Green)
  N6: Part10.D12_PWM, U2.DB7
  N7: Part10.D11_PWM, U2.DB6
  N8: Part10.D10_PWM, U2.DB5
  N9: Part10.D9_PWM, U2.DB4
  N10: Part10.D8_PWM, U2.E
  5V: Part10.5V, YwRobot_Power_Supply1.VCC#5, YwRobot_Power_Supply1.VCC#6, U2.VDD, R4.Pin_1, R5.leg1, SdModule2.5V
  GND: Part10.GND, YwRobot_Power_Supply1.GND#11, YwRobot_Power_Supply1.GND#12, U2.VSS, U2.R_W, U2.K, R5.leg2, SdModule2.GND
  N11: Part10.D2_PWM, Part12.S
  N12: Part10.D6_PWM, 7LEDDiskDFR3.DIN, 7LEDDiskDFR4.DIN
  N13: Part10.D7_PWM, U2.RS
  N14: Part10.D23, Keypad4x1.Pin1
  N15: Part10.D25, Keypad4x1.Pin2
  N16: Part10.D27, Keypad4x1.Pin3
  N17: Part10.D29, Keypad4x1.Pin4
  N18: Part10.D31, Keypad4x1.Pin5
  N19: Part10.D33, Keypad4x1.Pin6
  N20: Part10.D35, Keypad4x1.Pin7
  N21: Part10.D37, Keypad4x1.Pin8
  N22: Part10.D50, SdModule2.MISO
  N23: Part10.D51, SdModule2.MOSI
  N24: Part10.D52, SdModule2.SCK
  N25: Part10.D53, SdModule2.SS
  5V_2: YwRobot_Power_Supply1.VCC#9, YwRobot_Power_Supply1.VCC#10, 7LEDDiskDFR3.5V, 7LEDDiskDFR4.5V, J3.VCC_(Red), ZS-042_RTC3.VCC, Part11.5V, Part12.Vin
  GND_2: YwRobot_Power_Supply1.GND#13, YwRobot_Power_Supply1.GND#14, 7LEDDiskDFR3.GRN, 7LEDDiskDFR4.GRN, J3.GND_(Black), ZS-042_RTC3.GND, Part11.GND, Part12.-
  N26: U2.VO, R5.wiper
  N27: U2.A, R4.Pin_0

custom parts:
  YwRobot Breadboard Power Supply: The YwRobot Breadboard Power Supply (MB-V2) has two power rails; they can be 5V or 3V3. Power to the module can be provided through the female USB socket or through the A10 (female) 2.1mm power jack.
  Gravity Analog Sound Level Meter: In our environment, there are all kinds of sounds, some of which are quite noisy. With the development of human civilization, the quiet environments have become few and far between, and are replaced with more and more noisy environments instead. Staying in the loud places for long time will have an impact on hearing, which is bad for health. Sound level meter (also known as the decibel meter,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
  KY-022 Infrared Receiver Module: Arduino IR receiver module KY-022, based on 1838 IR Receiver/Decoder. It reacts to 38kHz infrared light.
  Membran Keypad 4x4: Membrane Keypad 4x4 Matrix
